# Fritzing sketch SSPMeteo-ESQUEMA (saved by Fritzing 0.9.2b)
circuit board: 3.50866cm x 5.31575cm

parts:
  DHT22 = Humidity and Temperature Sensor RHT03
  R1 = Resistor [tolerance=±5% resistance=10k package=THT]
  SSPMeteo = Arduino Uno (Rev3)
  Conector_RF433 = screw terminal, 3 pins
  Lluvia = Reed switch [package=THT]
  Anemometro = Reed switch [package=THT]
  Conector_sensores = screw terminal, 9 pins
  Veleta = Basic Flex Resistor
  R2 = Resistor [tolerance=±5% resistance=10k package=THT]

nets:
  VCC: DHT22.Vcc, R1.Pin_0, SSPMeteo.5V, Conector_sensores.pin4, Conector_sensores.pin5, Veleta.pin_1
  N1: DHT22.Data-signal, R1.Pin_1, SSPMeteo.D4, Conector_sensores.pin3
  N2: DHT22.GND_2, SSPMeteo.GND, Conector_RF433.pin1, Lluvia.pin_1, Anemometro.pin_1, Conector_sensores.pin6, Conector_sensores.pin7, Conector_sensores.pin8, R2.Pin_0
  N3: SSPMeteo.A0, Conector_sensores.pin9, Veleta.Pin_2, R2.Pin_1
  N4: SSPMeteo.D8, Conector_RF433.pin3
  N5: SSPMeteo.D2, Lluvia.pin_2, Conector_sensores.pin1
  N6: SSPMeteo.VIN, Conector_RF433.pin2
  N7: Anemometro.pin_2, Conector_sensores.pin2

notes:
  SSPMeteo
  T/H
  R
  5V
  GND
  WD
  WS
  DATA
  VCC
  RF433
  sensores
  NO VALIDO
