# Fritzing sketch SSPMeteo (saved by Fritzing 0.9.2b)
circuit board: 3.50866cm x 5.31575cm

parts:
  Rain_gauge = Reed switch [package=THT]
  DHT22 = Humidity and Temperature Sensor RHT03
  R2 = Resistor [tolerance=±5% resistance=10k package=THT]
  R1 = Resistor [tolerance=±5% resistance=10k package=THT]
  SSPMeteo = Arduino Uno (Rev3)
  Conector_RF433 = screw terminal, 3 pins
  Conector_sensores = screw terminal, 10 pins

nets:
  N1: Rain_gauge.pin_1, DHT22.GND_2, SSPMeteo.GND, Conector_RF433.pin1, Conector_sensores.pin5, Conector_sensores.pin6, Conector_sensores.pin7, Conector_sensores.pin8
  N2: Rain_gauge.pin_2, R1.Pin_1, SSPMeteo.D2, Conector_sensores.pin1
  VCC: DHT22.Vcc, R2.Pin_0, R1.Pin_0, SSPMeteo.5V, Conector_sensores.pin3, Conector_sensores.pin4
  N3: DHT22.Data-signal, R2.Pin_1, SSPMeteo.D4, Conector_sensores.pin2
  N4: SSPMeteo.A0, Conector_sensores.pin9
  N5: SSPMeteo.A1, Conector_sensores.pin10
  N6: SSPMeteo.D8, Conector_RF433.pin3
  N7: SSPMeteo.VIN, Conector_RF433.pin2

notes:
  SSPMeteo
  T/H
  R
  5V
  GND
  WD
  WS
  DATA
  VCC
  RF433
  sensores
