# Fritzing sketch ssp-ws (saved by Fritzing 0.9.2b)
circuit board: 5.49725cm x 5.33093cm

parts:
  Rain_gauge = Reed switch [package=THT]
  DHT22 = Humidity and Temperature Sensor RHT03
  R2 = Resistor [tolerance=±5% resistance=10k package=THT]
  R1 = Resistor [tolerance=±5% resistance=10k package=THT]
  Parte1 = Arduino Uno (Rev3)
  J3 = screw terminal, 10 pins
  J4 = screw terminal, 3 pins

nets:
  N1: Rain_gauge.pin_1, DHT22.GND_2, Parte1.GND, J3.pin5, J3.pin6, J3.pin7, J3.pin8, J4.pin3
  N2: Rain_gauge.pin_2, R1.Pin_1, Parte1.D2, J3.pin1
  VCC: DHT22.Vcc, R2.Pin_0, R1.Pin_0, Parte1.5V, J3.pin3, J3.pin4
  N3: DHT22.Data-signal, R2.Pin_1, Parte1.D4, J3.pin2
  N4: Parte1.A0, J3.pin9
  N5: Parte1.A1, J3.pin10
  N6: Parte1.D10_PWM/SS, J4.pin2
  N7: Parte1.VIN, J4.pin1

notes:
  SSPMeteo
  T/H
  R
  5V
  GND
  WD
  WS
  TX
  Vin
